// Logisim project hw3_circuit_inc_dec.circ as structural Verilog: 1 circuit, main circuit main
module main (
  input  a3,
  input  a2,
  input  a1,
  input  a0,
  input  b3,
  input  b2,
  input  b1,
  input  b0,
  input  control_bit_1,
  input  control_bit_2,
  output c_out,
  output s1,
  output s0,
  output s3,
  output s2
);

  wire adder_1_cout, adder_2_cout, adder_3_cout, and_1_out, and_2_out, and_3_out, not_1_out, or_1_out,
       xor_1_out, xor_2_out, xor_3_out, xor_4_out;

  and and_1 (and_1_out, b3, not_1_out);
  xor xor_1 (xor_1_out, and_1_out, control_bit_1);
  and and_2 (and_2_out, b2, not_1_out);
  xor xor_2 (xor_2_out, and_2_out, control_bit_1);
  and and_3 (and_3_out, b1, not_1_out);
  xor xor_3 (xor_3_out, and_3_out, control_bit_1);
  Adder #(.width(1)) adder_1 (.a(a0), .b(xor_4_out), .out(s0), .cin(control_bit_1), .cout(adder_1_cout));
  Adder #(.width(1)) adder_2 (.a(a1), .b(xor_3_out), .out(s1), .cin(adder_1_cout), .cout(adder_2_cout));
  Adder #(.width(1)) adder_3 (.a(a2), .b(xor_2_out), .out(s2), .cin(adder_2_cout), .cout(adder_3_cout));
  Adder #(.width(1)) adder_4 (.a(a3), .b(xor_1_out), .out(s3), .cin(adder_3_cout), .cout(c_out));
  or or_1 (or_1_out, b0, control_bit_2);
  xor xor_4 (xor_4_out, or_1_out, control_bit_1);
  not not_1 (not_1_out, control_bit_2);
endmodule
