// Logisim project hw4.circ as structural Verilog: 1 circuit, main circuit main
module main (
  input  X,
  output S2_prime,
  output S1_prime,
  output S0_prime,
  output Z
);

  wire and_1_out, and_2_out, and_3_out, and_4_out, and_5_out, and_6_out, and_7_out, clock_1_out, S0_q, S1_q,
       S2_q;

  Clock clock_1 (.out(clock_1_out));
  D_Flip_Flop S2 (.clk(clock_1_out), .D(S2_prime), .Q(S2_q));  // open: Qn, preset, en, reset
  D_Flip_Flop S1 (.clk(clock_1_out), .D(S1_prime), .Q(S1_q));  // open: Qn, preset, en, reset
  and and_1 (and_1_out, ~X, S0_q, S0_q);  // AND_Gate
  and and_2 (and_2_out, ~S2_q, S1_q, ~S0_q);  // AND_Gate
  and and_3 (and_3_out, S2_q, ~S0_q);  // AND_Gate
  and and_4 (and_4_out, ~S0_q, ~X);  // AND_Gate
  and and_5 (and_5_out, S0_q, X);
  and and_6 (and_6_out, S2_q, ~S1_q, ~X);  // AND_Gate
  and and_7 (and_7_out, S2_q, S1_q, X);
  D_Flip_Flop S0 (.clk(clock_1_out), .D(X), .Q(S0_q));  // open: Qn, preset, en, reset
  or u_Z (Z, and_6_out, and_7_out);
  or u_S2_prime (S2_prime, and_1_out, and_2_out, and_3_out);
  or u_S1_prime (S1_prime, and_4_out, and_5_out);

  assign S0_prime = X;

  // Notes on the sheet:
  //   James Guan
  //   Homework 4 Problem 4
  //   States (S2 S1 S0):
  //   000 = A
  //   001 = B
  //   010 = C
  //   011 = D
  //   100 = E
  //   101 = F
  //   110 = G
endmodule
